// Digital circuit 2Complement.dig as structural Verilog
module _2Complement (
  input  A0,
  input  A1,
  input  A2,
  input  A3,
  output S0,
  output S1,
  output S2,
  output S3,
  output Co
);

  wire fulladder_2_co, fulladder_3_co, fulladder_4_co, not_1_out, not_2_out, not_3_out, not_4_out;

  fullAdder fulladder_1 (.A(not_1_out), .B(1'b0), .Ci(fulladder_2_co), .Co(Co), .S(S3));
  not not_1 (not_1_out, A3);
  fullAdder fulladder_2 (.A(not_2_out), .B(1'b0), .Ci(fulladder_3_co), .Co(fulladder_2_co), .S(S2));
  not not_2 (not_2_out, A2);
  fullAdder fulladder_3 (.A(not_3_out), .B(1'b0), .Ci(fulladder_4_co), .Co(fulladder_3_co), .S(S1));
  not not_3 (not_3_out, A1);
  fullAdder fulladder_4 (.A(not_4_out), .B(1'b1), .Ci(1'b0), .Co(fulladder_4_co), .S(S0));
  not not_4 (not_4_out, A0);
endmodule

/* Test case 2Complement:
A0 A1 A2 A3 S0 S1 S2 S3 Co 

 0 0 0 0 0 0 0 0 1
 0 0 0 1 0 0 0 1 0
 0 0 1 0 0 0 1 1 0
 0 0 1 1 0 0 1 0 0
 0 1 0 0 0 1 1 1 0
 0 1 0 1 0 1 1 0 0
 0 1 1 0 0 1 0 1 0
 0 1 1 1 0 1 0 0 0
 1 0 0 0 1 1 1 1 0
 1 0 0 1 1 1 1 0 0
 1 0 1 0 1 1 0 1 0
 1 0 1 1 1 1 0 0 0
 1 1 0 0 1 0 1 1 0
 1 1 0 1 1 0 1 0 0
 1 1 1 0 1 0 0 1 0
 1 1 1 1 1 0 0 0 0
*/
