// Digital circuit 4bitsAdder.dig as structural Verilog
module _4bitsAdder (
  input  A0,
  input  B0,
  input  A1,
  input  B1,
  input  A2,
  input  B2,
  input  A3,
  input  B3,
  output S0,
  output S1,
  output S2,
  output S3,
  output Co
);

  wire fulladder_2_co, fulladder_3_co, fulladder_4_co;

  fullAdder fulladder_1 (.A(A3), .B(B3), .Ci(fulladder_2_co), .Co(Co), .S(S3));
  fullAdder fulladder_2 (.A(A2), .B(B2), .Ci(fulladder_3_co), .Co(fulladder_2_co), .S(S2));
  fullAdder fulladder_3 (.A(A1), .B(B1), .Ci(fulladder_4_co), .Co(fulladder_3_co), .S(S1));
  fullAdder fulladder_4 (.A(A0), .B(B0), .Ci(1'b0), .Co(fulladder_4_co), .S(S0));
endmodule
