// Digital circuit Complemento_2.dig as structural Verilog
module Complemento_2 (
  input  B0,
  input  B1,
  input  B2,
  input  B3,
  output S0,
  output S1,
  output S2,
  output S3
);

  wire inversor_1_nb0, inversor_1_nb1, inversor_1_nb2, inversor_1_nb3;

  Inversor inversor_1 (
    .B0(B0), .B1(B1), .B2(B2), .B3(B3), .nB0(inversor_1_nb0), .nB1(inversor_1_nb1), .nB2(inversor_1_nb2),
    .nB3(inversor_1_nb3));
  Semisumador_nibble semisumador_nibble_1 (
    .B0(inversor_1_nb0), .B1(inversor_1_nb1), .B2(inversor_1_nb2), .B3(inversor_1_nb3), .UNIDAD(1'b1),
    .S0(S0), .S1(S1), .S2(S2), .S3(S3));
endmodule
