// Digital circuit Inversor.dig as structural Verilog
module Inversor (
  input  B0,
  input  B1,
  input  B2,
  input  B3,
  output nB0,
  output nB1,
  output nB2,
  output nB3
);

  not not_1 (nB3, B3);
  not not_2 (nB2, B2);
  not not_3 (nB1, B1);
  not not_4 (nB0, B0);
endmodule
