// Digital circuit Multiplexor_8-4.dig as structural Verilog
module Multiplexor_8_4 (
  input  A3,
  input  A2,
  input  A1,
  input  A0,
  input  B3,
  input  B2,
  input  B1,
  input  B0,
  output C3,
  output C2,
  output C1,
  output C0
);

  wire not_1_out, or_1_out;

  or or_1 (or_1_out, B3, B2, B1, B0);
  not not_1 (not_1_out, or_1_out);
  and and_1 (C3, A3, not_1_out);
  and and_2 (C2, A2, not_1_out);
  and and_3 (C1, A1, not_1_out);
  and and_4 (C0, A0, not_1_out);
endmodule
