// Digital circuit Multiplexor_9-4.dig as structural Verilog
module Multiplexor_9_4 (
  input  A3,
  input  A2,
  input  A1,
  input  A0,
  input  B3,
  input  B2,
  input  B1,
  input  B0,
  input  Cin,
  output C3,
  output C2,
  output C1,
  output C0
);

  wire and_1_out, and_2_out, and_3_out, and_4_out, and_5_out, and_6_out, and_7_out, and_8_out, not_1_out;

  not not_1 (not_1_out, Cin);
  and and_1 (and_1_out, A3, Cin);
  and and_2 (and_2_out, A2, Cin);
  and and_3 (and_3_out, A1, Cin);
  and and_4 (and_4_out, A0, Cin);
  and and_5 (and_5_out, B3, not_1_out);
  and and_6 (and_6_out, B2, not_1_out);
  and and_7 (and_7_out, B1, not_1_out);
  and and_8 (and_8_out, B0, not_1_out);
  or or_1 (C3, and_1_out, and_5_out);
  or or_2 (C2, and_2_out, and_6_out);
  or or_3 (C1, and_3_out, and_7_out);
  or or_4 (C0, and_4_out, and_8_out);
endmodule
