// Digital circuit Restador01.dig as structural Verilog
module Restador01 (
  input  B3,
  input  A0,
  input  A1,
  input  A2,
  input  A3,
  input  B2,
  input  B1,
  input  B0,
  output S3,
  output S2,
  output S1,
  output S0
);

  wire complemento_2_1_s0, complemento_2_1_s1, complemento_2_1_s2, complemento_2_1_s3, complemento_2_2_s0,
       complemento_2_2_s1, complemento_2_2_s2, complemento_2_2_s3, multiplexor_8_4_1_c0,
       multiplexor_8_4_1_c1, multiplexor_8_4_1_c2, multiplexor_8_4_1_c3, multiplexor_9_4_2_c0,
       multiplexor_9_4_2_c1, multiplexor_9_4_2_c2, multiplexor_9_4_2_c3, nor_1_out, sumador_nibble_1_cout,
       sumador_nibble_1_s0, sumador_nibble_1_s1, sumador_nibble_1_s2, sumador_nibble_1_s3;

  Multiplexor_8_4 multiplexor_8_4_1 (
    .A3(A3), .A2(A2), .A1(A1), .A0(A0), .B3(B3), .B2(B2), .B1(B1), .B0(B0), .C3(multiplexor_8_4_1_c3),
    .C2(multiplexor_8_4_1_c2), .C1(multiplexor_8_4_1_c1), .C0(multiplexor_8_4_1_c0));
  nor nor_1 (nor_1_out, B0, B1, B2, B3);
  Complemento_2 complemento_2_1 (
    .B0(B0), .B1(B1), .B2(B2), .B3(B3), .S0(complemento_2_1_s0), .S1(complemento_2_1_s1),
    .S2(complemento_2_1_s2), .S3(complemento_2_1_s3));
  Multiplexor_9_4 multiplexor_9_4_1 (
    .A3(multiplexor_8_4_1_c3), .A2(multiplexor_8_4_1_c2), .A1(multiplexor_8_4_1_c1),
    .A0(multiplexor_8_4_1_c0), .B3(multiplexor_9_4_2_c3), .B2(multiplexor_9_4_2_c2),
    .B1(multiplexor_9_4_2_c1), .B0(multiplexor_9_4_2_c0), .Cin(nor_1_out), .C3(S3), .C2(S2), .C1(S1), .C0(S0));
  Sumador_nibble sumador_nibble_1 (
    .A0(A0), .B0(complemento_2_1_s0), .A1(A1), .B1(complemento_2_1_s1), .A2(A2), .B2(complemento_2_1_s2),
    .A3(A3), .B3(complemento_2_1_s3), .S0(sumador_nibble_1_s0), .S1(sumador_nibble_1_s1),
    .S2(sumador_nibble_1_s2), .S3(sumador_nibble_1_s3), .Cout(sumador_nibble_1_cout));
  Complemento_2 complemento_2_2 (
    .B0(sumador_nibble_1_s0), .B1(sumador_nibble_1_s1), .B2(sumador_nibble_1_s2), .B3(sumador_nibble_1_s3),
    .S0(complemento_2_2_s0), .S1(complemento_2_2_s1), .S2(complemento_2_2_s2), .S3(complemento_2_2_s3));
  Multiplexor_9_4 multiplexor_9_4_2 (
    .A3(sumador_nibble_1_s3), .A2(sumador_nibble_1_s2), .A1(sumador_nibble_1_s1), .A0(sumador_nibble_1_s0),
    .B3(complemento_2_2_s3), .B2(complemento_2_2_s2), .B1(complemento_2_2_s1), .B0(complemento_2_2_s0),
    .Cin(sumador_nibble_1_cout), .C3(multiplexor_9_4_2_c3), .C2(multiplexor_9_4_2_c2),
    .C1(multiplexor_9_4_2_c1), .C0(multiplexor_9_4_2_c0));
endmodule
