// Digital circuit Semisumador_nibble.dig as structural Verilog
module Semisumador_nibble (
  input  B0,
  input  B1,
  input  B2,
  input  B3,
  input  UNIDAD,
  output S0,
  output S1,
  output S2,
  output S3
);

  wire semisumador_2_c, semisumador_3_c, semisumador_4_c;

  Semisumador semisumador_1 (.A(B3), .B(semisumador_2_c), .S(S3));  // open: C
  Semisumador semisumador_2 (.A(B2), .B(semisumador_3_c), .C(semisumador_2_c), .S(S2));
  Semisumador semisumador_3 (.A(B1), .B(semisumador_4_c), .C(semisumador_3_c), .S(S1));
  Semisumador semisumador_4 (.A(B0), .B(UNIDAD), .C(semisumador_4_c), .S(S0));
endmodule
