// Digital circuit Sumador.dig as structural Verilog
module Sumador (
  input  A,
  input  B,
  input  Cin,
  output C,
  output S
);

  wire semisumador_1_c, semisumador_1_s, semisumador_2_c;

  Semisumador semisumador_1 (.A(A), .B(B), .C(semisumador_1_c), .S(semisumador_1_s));
  Semisumador semisumador_2 (.A(semisumador_1_s), .B(Cin), .C(semisumador_2_c), .S(S));
  or or_1 (C, semisumador_1_c, semisumador_2_c);
endmodule

/* Test case:
A B Cin		C S
0 0 0  		0 0 
0 0 1		0 1
0 1 0		0 1
0 1 1		1 0
1 0 0		0 1
1 0 1		1 0
1 1 0		1 0
1 1 1		1 1
*/
