// Digital circuit Sumador_nibble.dig as structural Verilog
module Sumador_nibble (
  input  A0,
  input  B0,
  input  A1,
  input  B1,
  input  A2,
  input  B2,
  input  A3,
  input  B3,
  output S0,
  output S1,
  output S2,
  output S3,
  output Cout
);

  wire sumador_2_c, sumador_3_c, sumador_4_c;

  Sumador sumador_1 (.A(A3), .B(B3), .Cin(sumador_2_c), .C(Cout), .S(S3));
  Sumador sumador_2 (.A(A2), .B(B2), .Cin(sumador_3_c), .C(sumador_2_c), .S(S2));
  Sumador sumador_3 (.A(A1), .B(B1), .Cin(sumador_4_c), .C(sumador_3_c), .S(S1));
  Sumador sumador_4 (.A(A0), .B(B0), .Cin(1'b0), .C(sumador_4_c), .S(S0));
endmodule
