// Digital circuit fullAdder.dig as structural Verilog
module fullAdder (
  input  A,
  input  B,
  input  Ci,
  output Co,
  output S
);

  wire halfadder_1_co, halfadder_1_s, halfadder_2_co;

  halfAdder halfadder_1 (.A(A), .B(B), .Co(halfadder_1_co), .S(halfadder_1_s));
  halfAdder halfadder_2 (.A(halfadder_1_s), .B(Ci), .Co(halfadder_2_co), .S(S));
  or or_1 (Co, halfadder_1_co, halfadder_2_co);
endmodule

/* Test case FullAdder:
A B Ci Co S 

 0 0 0 0 0
 0 0 1 0 1
 0 1 0 0 1
 0 1 1 1 0
 1 0 0 0 1
 1 0 1 1 0
 1 1 0 1 0
 1 1 1 1 1
*/
