// Digital circuit halfAdder.dig as structural Verilog
module halfAdder (
  input  A,
  input  B,
  output Co,
  output S
);

  and and_1 (Co, A, B);
  xor xor_1 (S, A, B);
endmodule

/* Test case HalfAdder:
A B Suma COut 

 0 0 0 0
 0 1 1 0
 1 0 1 0
 1 1 0 1
*/
